# Fritzing sketch ESP8266simpleTest (saved by Fritzing 0.9.2b)
breadboards: 1

parts:
  U1 = ESP8266 WiFi Module [part_number=ESP8266]
  R1 = Resistor [tolerance=±5% resistance=1.8k package="0603 [SMD]"]
  R2 = Resistor [tolerance=±5% resistance=1.2k package=THT]

nets:
  N1: U1.RXD, R1.Pin_1, R2.Pin_0
  N2: U1.VCC, U1.RST, U1.GPIO_2, U1.CH_PD
  N3: U1.GND, R1.Pin_0

custom parts:
  ESP8266 WiFi Module: Generic WiFi Module based on the ESP8266 with onboard PCB antenna and UART communications
